# Fritzing sketch PiPower HAT (saved by Fritzing 0.9.3b)
circuit board: 6.52541cm x 5.62539cm
breadboards: 1

parts:
  Part1 = Arduino Pro Mini (5V)
  U2 = Voltage Regulator - 5V [package="TO220 [THT]"]  # not connected
  U1 = Voltage Regulator - 5V [package="DPak [SMD]"]  # not connected
  U3 = G3VM-61E1 [package=g3vm-61e1]  # not connected
  JACK2 = 2.1mm DC Barrel Jack
  JACK1 = USB_AB [package=usb-ab-micro-smd]  # not connected
  J1 = Cobbler Plus Cable
  Button = male pin header, 4 pins [form="♂ (male)"]  # not connected

nets:
  N1: Part1.RAW, JACK2.center
  N2: Part1.GND, JACK2.sleeve, J1.GND#8, J1.GND#24, J1.GND#38
  N3: Part1.VCC, J1.5.0V#3
  N4: Part1.RXI, J1.TXD
  N5: Part1.TXO, J1.RXD

custom parts:
  2.1mm DC Barrel Jack: 2.1mm DC Barrel Jack with Thru-Hole Connectors (breadboardable)
  Cobbler Plus Cable: The Cobbler Plus is an add on prototyping board from Adafruit specifically designed for the Raspberry Pi B+ that can break out all those tasty power, GPIO, I2C and SPI pins from the 40-pin header onto a solderless breadboard. This set will make "cobbling together" prototypes with the Pi super easy. The Cobbler Plus can plug into any solderless breadboard.
